# Fritzing sketch Schematic_ExternalSensor (saved by Fritzing 1.0.8)
breadboards: 1

parts:
  U1 = XIAO ESP32C6 [part_number=" XIAO ESP32C6"]
  DHT1 = DHT22 Humidity and Temperature Sensor
  YL-1 = YL-38 Humitidy Sensor
  U2 = LIPO-2000mAh [package=lipo-2000]
  R1 = Resistor [tolerance=±5% power=0.25W resistance=220k package=THT]
  R2 = Resistor [tolerance=±5% power=0.25W resistance=220k package=THT]

nets:
  N1: U1.D0, R1.Pin_1, R2.Pin_0
  N2: U1.D1, YL-1.ANALOG
  VDD: U1.D3, DHT1.VDD, YL-1.VCC
  N3: U1.D9, YL-1.DIGITAL
  N4: U1.D10, DHT1.DATA
  GND: U1.GND, DHT1.GND, YL-1.GND
  N5: U2.+, R1.Pin_0
  N6: U2.-, R2.Pin_1

notes:
  on the other side of that µC two pads are exposed for connecting the battery. these are not present in the fritzing part file
  Pin wake up is only supported on pins D0..D3

custom parts:
  XIAO ESP32C6: XIAO ESP32C6 is a cost-effective MCU based on Espressif’s ESP32-C6. This compact MCU excels in Matter-compliant smart home applications with its support for various wireless connectivity (2.4GHz Wi-Fi 6, BLE 5.0, Zigbee, and Thread). Designed with the thumb-size footprint and a single-sided mount of the XIAO Series, it's perfect for space-limited projects. Encrypted on the chip, the XIAO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
